# Fritzing sketch Cardinodroid Finish Line Fritzing Sketch (saved by Fritzing 0.9.2b)
circuit board: 8.46667cm x 5.64444cm
breadboards: 1

parts:
  Part1 = Arduino Uno (Rev3)
  R1 = Resistor [tolerance=±5% resistance=1k package="1206 [SMD]"]
  U4 = CUSTOM PRESSURE SENSOR
  U5 = LCD-16X2 [package=lcd-8x2]
  R2 = Trimmer Potentiometer [maximum_resistance=10kΩ package=THT]
  R3 = Resistor [tolerance=±5% resistance=220 package=THT]

nets:
  N1: Part1.A5/SCL, R1.Pin_1, U4.VIN
  N2: Part1.D11_PWM/MOSI, U5.E
  N3: Part1.D12/MISO, U5.RS
  GND: Part1.GND, U4.GND, U5.VSS, U5.R_W, U5.K, R2.leg1
  N4: Part1.D2, U5.DB7
  N5: Part1.D3_PWM, U5.DB6
  N6: Part1.D4, U5.DB5
  N7: Part1.D5_PWM, U5.DB4
  5V: Part1.5V, R1.Pin_0, U5.VDD, R2.leg2, R3.Pin_0
  N8: U5.VO, R2.wiper
  N9: U5.A, R3.Pin_1

notes:
  Pressure sensor
  Pressure plate switch

custom parts:
  CUSTOM PRESSURE SENSOR: Custom pressure sensor using cardboard and aluminium foil.
