# Fritzing sketch Carduinodroid finish line timer (saved by Fritzing 0.9.2b)
breadboards: 1

parts:
  Part1 = Arduino Uno (Rev3)
  U5 = LCD-16X2 [package=lcd-8x2]
  S1 = Pushbutton [package="[THT]"]
  S2 = Pushbutton [package="[THT]"]
  S3 = Pushbutton [package="[THT]"]
  S4 = Pushbutton [package="[THT]"]
  J1 = Piezo Speaker
  S5 = Pushbutton [package="[THT]"]
  S6 = Pushbutton [package="[THT]"]
  S7 = Pushbutton [package="[THT]"]

nets:
  N1: Part1.D11_PWM/MOSI, U5.E
  N2: Part1.D12/MISO, U5.RS
  N3: Part1.GND, S1.Pin_1, S1.Pin_2, S2.Pin_1, S2.Pin_2, S3.Pin_1, S3.Pin_2, S4.Pin_1, S4.Pin_2, J1.pin1, S5.Pin_1, S5.Pin_2, S6.Pin_1, S6.Pin_2, S7.Pin_1, S7.Pin_2
  N4: Part1.D2, U5.DB7
  N5: Part1.D3_PWM, U5.DB6
  N6: Part1.D4, U5.DB5
  N7: Part1.D5_PWM, U5.DB4, J1.pin2
  5V: Part1.5V, U5.VDD
  N8: U5.VSS, U5.R_W, U5.K
  N9: S1.Pin_3, S1.Pin_4, S2.Pin_3, S2.Pin_4, S3.Pin_3, S3.Pin_4, S4.Pin_3, S4.Pin_4, S5.Pin_3, S5.Pin_4, S6.Pin_3, S6.Pin_4, S7.Pin_3, S7.Pin_4
